# Fritzing sketch EsquemaJoyStick (saved by Fritzing 0.9.3b)
breadboards: 1

parts:
  BeagleBone1 = BeagleBone Black
  U1 = POT [package=pot_alpha_rv16af-20]
  S1 = Momentary Switch [package=ksa_sealed_tac_switch]
  S2 = Momentary Switch [package=ksa_sealed_tac_switch]
  R1 = Photocell (LDR) [package=THT]
  R2 = Resistor [tolerance=±5% resistance=220 package=THT]

nets:
  N1: BeagleBone1.no_name_yet#4, U1.S, S1.2, S2.2, R2.Pin_1
  N2: BeagleBone1.no_name_yet#11, S2.4
  N3: BeagleBone1.no_name_yet#12, S1.4
  N4: BeagleBone1.no_name_yet#38, U1.E
  N5: BeagleBone1.no_name_yet#39, BeagleBone1.no_name_yet#42, R1.pin_0
  N6: BeagleBone1.no_name_yet#40, U1.A

custom parts:
  BeagleBone Black: BeagleBone Black rev. A5B
